// Logisim project Design.circ as structural Verilog: 4 circuits, main circuit main
module main (
);

  wire and_1_out, and_2_out, and_3_out, and_4_out, clk, demultiplexer_1_out0, demultiplexer_1_out1, not_1_out;
  wire [1:0] counter_1_q;
  wire [2:0] IR_q2;
  wire [4:0] RA, RB, RC;
  wire [13:0] register_2_q_2, X;
  wire [31:0] ALU_out_5, mem_data, multiplexer_1_out, multiplexer_2_out, RC_data, register_1_q, register_4_q,
       register_file_1_ra, register_file_1_rb;
  wire [31:14] register_2_q, shift_register_1_q17;

  Counter #(.width(2), .max('h3)) counter_1 (.count(1'b1), .Q(counter_1_q), .clk(clk));  // open: load, D, carry, clr
  and and_1 (and_1_out, IR_q2[0], IR_q2[1], IR_q2[2]);
  and and_2 (and_2_out, ~IR_q2[0], ~IR_q2[1], IR_q2[2]);  // AND_Gate
  and and_3 (and_3_out, ~IR_q2[0], IR_q2[1], IR_q2[2]);  // AND_Gate
  and and_4 (and_4_out, IR_q2[1], counter_1_q[1], IR_q2[2]);
  Demultiplexer #(.disabled(0)) demultiplexer_1 (
    .out0(demultiplexer_1_out0), .out1(demultiplexer_1_out1), .in(1'b1), .sel(IR_q2[0]), .en(1'b1));
  not not_1 (not_1_out, and_1_out);
  Clock clock_1 (.out(clk));
  Register_File register_file_1 (
    .DMUX_ENABLE(not_1_out), .MUX_ENABLE(1'b1), .CLOCK(clk), .ADDRESS_C(RC), .C(RC_data),
    .RA(register_file_1_ra), .RB(register_file_1_rb), .ADDRESS_RA(RA), .ADDRESS_RB(RB));
  Register #(.width(32)) register_1 (.D(register_file_1_ra), .en(1'b1), .Q(register_1_q), .clk(clk));  // open: clr
  ALU ALU (.Select(IR_q2), .Enable(1'b1), .RA(register_1_q), .RB(multiplexer_2_out), .out_5(ALU_out_5));
  Register #(.width(32)) register_2 (
    .D(ALU_out_5), .en(1'b1), .Q({register_2_q, register_2_q_2}), .clk(clk));  // open: clr
  Multiplexer #(.width(32), .disabled(0)) multiplexer_1 (
    .in0({register_2_q, register_2_q_2}), .in1(mem_data), .out(multiplexer_1_out), .sel(and_3_out), .en(1'b1));
  Register #(.width(32)) register_3 (.D(multiplexer_1_out), .en(1'b1), .Q(RC_data), .clk(clk));  // open: clr
  Register #(.width(32)) register_4 (.D(register_file_1_rb), .en(1'b1), .Q(register_4_q), .clk(clk));  // open: clr
  Multiplexer #(.width(32), .disabled(0)) multiplexer_2 (
    .in0(register_4_q), .in1({shift_register_1_q17, X}), .out(multiplexer_2_out), .sel(and_2_out), .en(1'b1));
  Shift_Register #(.length(32)) IR (
    .shift(1'b0), .clk(clk), .q0(IR_q2[2]), .q1(IR_q2[1]), .q2(IR_q2[0]), .q3(RA[4]), .q4(RA[3]), .q5(RA[2]),
    .q6(RA[1]), .q7(RA[0]), .q8(RC[4]), .q9(RC[3]), .q10(RC[2]), .q11(RC[1]), .q12(RC[0]), .q13(RB[4]),
    .q14(RB[3]), .q15(RB[2]), .q16(RB[1]), .q17(RB[0]), .q18(X[13]), .q19(X[12]), .q20(X[11]), .q21(X[10]),
    .q22(X[9]), .q23(X[8]), .q24(X[7]), .q25(X[6]), .q26(X[5]), .q27(X[4]), .q28(X[3]), .q29(X[2]),
    .q30(X[1]), .q31(X[0]));  // open: in, out, load, clr, d0, d1, d2, d3, d4, d5, d6, d7, d8, d9, d10, d11, d12, d13, d14, d15, d16, d17, d18, d19, d20, d21, d22, d23, d24, d25, d26, d27, d28, d29, d30, d31
  Shift_Register #(.length(18)) shift_register_1 (
    .shift(1'b0), .clk(clk), .q0(shift_register_1_q17[31]), .q1(shift_register_1_q17[30]),
    .q2(shift_register_1_q17[29]), .q3(shift_register_1_q17[28]), .q4(shift_register_1_q17[27]),
    .q5(shift_register_1_q17[26]), .q6(shift_register_1_q17[25]), .q7(shift_register_1_q17[24]),
    .q8(shift_register_1_q17[23]), .q9(shift_register_1_q17[22]), .q10(shift_register_1_q17[21]),
    .q11(shift_register_1_q17[20]), .q12(shift_register_1_q17[19]), .q13(shift_register_1_q17[18]),
    .q14(shift_register_1_q17[17]), .q15(shift_register_1_q17[16]), .q16(shift_register_1_q17[15]),
    .q17(shift_register_1_q17[14]));  // open: in, out, load, clr, d0, d1, d2, d3, d4, d5, d6, d7, d8, d9, d10, d11, d12, d13, d14, d15, d16, d17
  RAM #(.addrWidth(14), .dataWidth(32), .bus("separate")) ram_1 (
    .addr(register_2_q_2), .din(register_4_q), .data(mem_data), .str(demultiplexer_1_out0), .sel(and_4_out),
    .clk(clk), .ld(demultiplexer_1_out1));  // open: clr
endmodule

module Register_File (
  input  DMUX_ENABLE,
  input  [4:0] ADDRESS_RA,
  input  [4:0] ADDRESS_C,
  input  MUX_ENABLE,
  input  [4:0] ADDRESS_RB,
  input  [31:0] C,
  input  CLOCK,
  output [31:0] RA,
  output [31:0] RB
);

  wire clock_1_out, demultiplexer_1_out0, demultiplexer_1_out1, demultiplexer_1_out2, demultiplexer_1_out3,
       demultiplexer_1_out4, demultiplexer_1_out5, demultiplexer_1_out6, demultiplexer_1_out7;
  wire [7:0] demultiplexer_1_out8, demultiplexer_1_out16, demultiplexer_1_out24;
  wire [31:0] R0_2_q, R0_3_q, R0_4_q, R0_5_q, R0_6_q, R0_7_q, R0_8_q, R0_9_q, R0_10_q, R0_11_q, R0_12_q,
       R0_13_q, R0_14_q, R0_15_q, R0_16_q, R0_17_q, R0_18_q, R0_19_q, R0_20_q, R0_21_q, R0_22_q, R0_23_q,
       R0_24_q, R0_25_q, R0_q, R1_q, R2_q, R3_q, R4_q, R5_q, R6_q, R7_q;

  Demultiplexer #(.select(5), .disabled(0)) demultiplexer_1 (
    .out0(demultiplexer_1_out0), .out1(demultiplexer_1_out1), .out2(demultiplexer_1_out2),
    .out3(demultiplexer_1_out3), .out4(demultiplexer_1_out4), .out5(demultiplexer_1_out5),
    .out6(demultiplexer_1_out6), .out7(demultiplexer_1_out7), .out8(demultiplexer_1_out8[0]),
    .out9(demultiplexer_1_out8[1]), .out10(demultiplexer_1_out8[2]), .out11(demultiplexer_1_out8[3]),
    .out12(demultiplexer_1_out8[4]), .out13(demultiplexer_1_out8[5]), .out14(demultiplexer_1_out8[6]),
    .out15(demultiplexer_1_out8[7]), .out16(demultiplexer_1_out16[0]), .out17(demultiplexer_1_out16[1]),
    .out18(demultiplexer_1_out16[2]), .out19(demultiplexer_1_out16[3]), .out20(demultiplexer_1_out16[4]),
    .out21(demultiplexer_1_out16[5]), .out22(demultiplexer_1_out16[6]), .out23(demultiplexer_1_out16[7]),
    .out24(demultiplexer_1_out24[0]), .out25(demultiplexer_1_out24[1]), .out26(demultiplexer_1_out24[2]),
    .out27(demultiplexer_1_out24[3]), .out28(demultiplexer_1_out24[4]), .out29(demultiplexer_1_out24[5]),
    .out30(demultiplexer_1_out24[6]), .out31(demultiplexer_1_out24[7]), .in(DMUX_ENABLE), .sel(ADDRESS_C),
    .en(DMUX_ENABLE));
  Clock clock_1 (.out(clock_1_out));
  Register #(.width(32)) R0 (.D(C), .en(demultiplexer_1_out0), .Q(R0_q), .clk(CLOCK));  // open: clr
  Register #(.width(32)) R0_2 (.D(C), .en(demultiplexer_1_out8[0]), .Q(R0_2_q), .clk(CLOCK));  // open: clr
  Register #(.width(32)) R0_3 (.D(C), .en(demultiplexer_1_out16[0]), .Q(R0_3_q), .clk(CLOCK));  // open: clr
  Register #(.width(32)) R0_4 (.D(C), .en(demultiplexer_1_out24[0]), .Q(R0_4_q), .clk(CLOCK));  // open: clr
  Register #(.width(32)) R1 (.D(C), .en(demultiplexer_1_out1), .Q(R1_q), .clk(CLOCK));  // open: clr
  Register #(.width(32)) R0_5 (.D(C), .en(demultiplexer_1_out8[1]), .Q(R0_5_q), .clk(CLOCK));  // open: clr
  Register #(.width(32)) R0_6 (.D(C), .en(demultiplexer_1_out16[1]), .Q(R0_6_q), .clk(CLOCK));  // open: clr
  Register #(.width(32)) R0_7 (.D(C), .en(demultiplexer_1_out24[1]), .Q(R0_7_q), .clk(CLOCK));  // open: clr
  Register #(.width(32)) R2 (.D(C), .en(demultiplexer_1_out2), .Q(R2_q), .clk(CLOCK));  // open: clr
  Register #(.width(32)) R0_8 (.D(C), .en(demultiplexer_1_out8[2]), .Q(R0_8_q), .clk(CLOCK));  // open: clr
  Register #(.width(32)) R0_9 (.D(C), .en(demultiplexer_1_out16[2]), .Q(R0_9_q), .clk(CLOCK));  // open: clr
  Register #(.width(32)) R0_10 (.D(C), .en(demultiplexer_1_out24[2]), .Q(R0_10_q), .clk(CLOCK));  // open: clr
  Register #(.width(32)) R3 (.D(C), .en(demultiplexer_1_out3), .Q(R3_q), .clk(CLOCK));  // open: clr
  Register #(.width(32)) R0_11 (.D(C), .en(demultiplexer_1_out8[3]), .Q(R0_11_q), .clk(CLOCK));  // open: clr
  Register #(.width(32)) R0_12 (.D(C), .en(demultiplexer_1_out16[3]), .Q(R0_12_q), .clk(CLOCK));  // open: clr
  Register #(.width(32)) R0_13 (.D(C), .en(demultiplexer_1_out24[3]), .Q(R0_13_q), .clk(CLOCK));  // open: clr
  Register #(.width(32)) R4 (.D(C), .en(demultiplexer_1_out4), .Q(R4_q), .clk(CLOCK));  // open: clr
  Register #(.width(32)) R0_14 (.D(C), .en(demultiplexer_1_out8[4]), .Q(R0_14_q), .clk(CLOCK));  // open: clr
  Register #(.width(32)) R0_15 (.D(C), .en(demultiplexer_1_out16[4]), .Q(R0_15_q), .clk(CLOCK));  // open: clr
  Register #(.width(32)) R0_16 (.D(C), .en(demultiplexer_1_out24[4]), .Q(R0_16_q), .clk(CLOCK));  // open: clr
  Register #(.width(32)) R5 (.D(C), .en(demultiplexer_1_out5), .Q(R5_q), .clk(CLOCK));  // open: clr
  Register #(.width(32)) R0_17 (.D(C), .en(demultiplexer_1_out8[5]), .Q(R0_17_q), .clk(CLOCK));  // open: clr
  Register #(.width(32)) R0_18 (.D(C), .en(demultiplexer_1_out16[5]), .Q(R0_18_q), .clk(CLOCK));  // open: clr
  Register #(.width(32)) R0_19 (.D(C), .en(demultiplexer_1_out24[5]), .Q(R0_19_q), .clk(CLOCK));  // open: clr
  Register #(.width(32)) R6 (.D(C), .en(demultiplexer_1_out6), .Q(R6_q), .clk(CLOCK));  // open: clr
  Register #(.width(32)) R0_20 (.D(C), .en(demultiplexer_1_out8[6]), .Q(R0_20_q), .clk(CLOCK));  // open: clr
  Register #(.width(32)) R0_21 (.D(C), .en(demultiplexer_1_out16[6]), .Q(R0_21_q), .clk(CLOCK));  // open: clr
  Register #(.width(32)) R0_22 (.D(C), .en(demultiplexer_1_out24[6]), .Q(R0_22_q), .clk(CLOCK));  // open: clr
  Register #(.width(32)) R7 (.D(C), .en(demultiplexer_1_out7), .Q(R7_q), .clk(CLOCK));  // open: clr
  Register #(.width(32)) R0_23 (.D(C), .en(demultiplexer_1_out8[7]), .Q(R0_23_q), .clk(CLOCK));  // open: clr
  Register #(.width(32)) R0_24 (.D(C), .en(demultiplexer_1_out16[7]), .Q(R0_24_q), .clk(CLOCK));  // open: clr
  Register #(.width(32)) R0_25 (.D(C), .en(demultiplexer_1_out24[7]), .Q(R0_25_q), .clk(CLOCK));  // open: clr
  Multiplexer #(.select(5), .width(32), .disabled(0)) multiplexer_1 (
    .in0(R0_q), .in1(R1_q), .in2(R2_q), .in3(R3_q), .in4(R4_q), .in5(R5_q), .in6(R6_q), .in7(R7_q),
    .in8(R0_2_q), .in9(R0_5_q), .in10(R0_8_q), .in11(R0_11_q), .in12(R0_14_q), .in13(R0_17_q),
    .in14(R0_20_q), .in15(R0_23_q), .in16(R0_3_q), .in17(R0_6_q), .in18(R0_9_q), .in19(R0_12_q),
    .in20(R0_15_q), .in21(R0_18_q), .in22(R0_21_q), .in23(R0_24_q), .in24(R0_4_q), .in25(R0_7_q),
    .in26(R0_10_q), .in27(R0_13_q), .in28(R0_16_q), .in29(R0_19_q), .in30(R0_22_q), .in31(R0_25_q), .out(RA),
    .sel(ADDRESS_RA), .en(MUX_ENABLE));
  Multiplexer #(.select(5), .width(32), .disabled(0)) multiplexer_2 (
    .in0(R0_q), .in1(R1_q), .in2(R2_q), .in3(R3_q), .in4(R4_q), .in5(R5_q), .in6(R6_q), .in7(R7_q),
    .in8(R0_2_q), .in9(R0_5_q), .in10(R0_8_q), .in11(R0_11_q), .in12(R0_14_q), .in13(R0_17_q),
    .in14(R0_20_q), .in15(R0_23_q), .in16(R0_3_q), .in17(R0_6_q), .in18(R0_9_q), .in19(R0_12_q),
    .in20(R0_15_q), .in21(R0_18_q), .in22(R0_21_q), .in23(R0_24_q), .in24(R0_4_q), .in25(R0_7_q),
    .in26(R0_10_q), .in27(R0_13_q), .in28(R0_16_q), .in29(R0_19_q), .in30(R0_22_q), .in31(R0_25_q), .out(RB),
    .sel(ADDRESS_RB), .en(MUX_ENABLE));

  // Notes on the sheet:
  //   DMUX_ENABLE: pull=up
endmodule

module ALU (
  input  [31:0] RA,
  input  [31:0] RB,
  input  [2:0] Select,
  input  Enable,
  output [31:0] out_5
);

  wire [31:0] adder_1_out, and_1_out, or_1_out, subtractor_1_out;

  Adder #(.width(32)) adder_1 (.a(RA), .b(RB), .out(adder_1_out));  // open: cin, cout
  Subtractor #(.width(32)) subtractor_1 (.a(RA), .b(RB), .out(subtractor_1_out));  // open: bin, bout
  assign and_1_out = RA & RB;  // AND_Gate and_1, 32 bits wide
  assign or_1_out = RA | RB;  // OR_Gate or_1, 32 bits wide
  Multiplexer #(.select(3), .width(32), .disabled(0)) multiplexer_1 (
    .in0(adder_1_out), .in1(subtractor_1_out), .in2(and_1_out), .in3(or_1_out), .in4(RB), .in5(RB), .in6(RB),
    .in7(RB), .out(out_5), .sel(Select), .en(Enable));
endmodule

module Instruction_Address_Generator (
  input  mux_inc_select,
  input  [31:0] RA,
  input  [31:0] _2,
  input  mux_pc_select,
  input  [31:0] Offset,
  input  mux_enable,
  input  pc_enable,
  input  clock,
  input  [31:0] PC
);

  wire [31:0] adder_1_out, multiplexer_1_out, multiplexer_2_out;

  Register #(.width(32)) register_1 (.D(PC), .en(pc_enable), .clk(clock));  // open: Q, clr
  Multiplexer #(.width(32)) multiplexer_1 (
    .in0(RA), .in1(adder_1_out), .out(multiplexer_1_out), .sel(mux_pc_select), .en(mux_enable));
  Register #(.width(32)) register_2 (.D(multiplexer_1_out), .en(pc_enable), .Q(PC), .clk(clock));  // open: clr
  Adder #(.width(32)) adder_1 (.a(multiplexer_2_out), .b(PC), .out(adder_1_out));  // open: cin, cout
  Multiplexer #(.width(32)) multiplexer_2 (
    .in0(_2), .in1(Offset), .out(multiplexer_2_out), .sel(mux_inc_select), .en(mux_enable));
endmodule
